// Logisim project 2421_Parity Generator.circ as structural Verilog: 1 circuit, main circuit main
module main (
  input  [3:0] in_1,
  output out_2
);

  wire xor_1_out, xor_2_out;

  xor xor_1 (xor_1_out, in_1[0], in_1[1]);
  xor xor_2 (xor_2_out, xor_1_out, in_1[2]);
  xor xor_3 (out_2, xor_2_out, in_1[3]);
endmodule
