// Logisim project CA.circ as structural Verilog: 4 circuits, main circuit main
module main (
  input  in_1,
  input  [1:0] in_2
);

  wire and_1_out, button_1_out, clock_1_out, clock_2_out, clock_3_out, clock_4_out, clock_5_out,
       multiplexer_1_out;
  wire [3:0] counter_1_q, counter_2_q, counter_3_q;
  wire [15:0] main_1_p2, main_1_p3, main_1_p4, main_1_p5, main_1_p6, main_1_p7, main_1_p8, main_1_p9,
       main_1_p10, main_1_p11, main_1_p12, main_1_p13, main_1_p14, main_1_p15, main_1_p16, main_1_p17,
       main_1_p18, main_1_p19, main_1_p20, main_1_p21, main_1_p22, main_1_p23, main_1_p24, main_1_p25,
       main_1_p26, main_1_p27, main_1_p28, main_1_p29, main_1_p30, main_1_p31, main_1_p32, main_1_p33,
       main_1_p34, rom_1_data;

  Clock clock_1 (.out(clock_1_out));
  Clock #(.highDuration(2), .lowDuration(2)) clock_2 (.out(clock_2_out));
  Clock #(.highDuration(3), .lowDuration(3)) clock_3 (.out(clock_3_out));
  Clock #(.highDuration(4), .lowDuration(4)) clock_4 (.out(clock_4_out));
  Counter #(.width(4), .max('hf)) counter_1 (
    .Q(counter_1_q), .clk(multiplexer_1_out), .clr(button_1_out));  // open: load, D, count, carry
  Multiplexer #(.select(2)) multiplexer_1 (
    .in0(clock_1_out), .in1(clock_2_out), .in2(clock_3_out), .in3(clock_4_out), .out(multiplexer_1_out),
    .sel(in_2));  // open: en
  Counter #(.width(4), .max('hf)) counter_2 (
    .D(4'b0010), .Q(counter_2_q), .clk(clock_5_out), .clr(button_1_out));  // open: load, count, carry
  Clock clock_5 (.out(clock_5_out));
  ROM #(.addrWidth(4), .dataWidth(16)) rom_1 (.addr(counter_2_q), .data(rom_1_data));  // open: sel
  Counter #(.width(4), .max('hf)) counter_3 (
    .load(in_1), .Q(counter_3_q), .clk(clock_5_out), .clr(button_1_out));  // open: D, count, carry
  Button button_1 (.out(button_1_out));
  and and_1 (and_1_out, rom_1_data[0], clock_5_out);
  DotMatrix #(.matrixcols(16), .matrixrows(16)) dotmatrix_1 (
    .col0(main_1_p3), .col1(main_1_p5), .col2(main_1_p7), .col3(main_1_p9), .col4(main_1_p11),
    .col5(main_1_p13), .col6(main_1_p15), .col7(main_1_p17), .col8(main_1_p19), .col9(main_1_p21),
    .col10(main_1_p23), .col11(main_1_p25), .col12(main_1_p27), .col13(main_1_p29), .col14(main_1_p31),
    .col15(main_1_p33));
  // GPU__1__main main_1: pin names not known; wires that end beside it: and_1_out, main_1_p2[0], main_1_p3, main_1_p4, main_1_p5, main_1_p6, main_1_p7, main_1_p8, main_1_p9, main_1_p10, main_1_p11, main_1_p12, main_1_p13, main_1_p14, main_1_p15, main_1_p16, main_1_p17, main_1_p18, main_1_p19, main_1_p20, main_1_p21, main_1_p22, main_1_p23, main_1_p24, main_1_p25, main_1_p26, main_1_p27, main_1_p28, main_1_p29, main_1_p30, main_1_p31, main_1_p32, main_1_p33, main_1_p34
  Decoder #(.select(4)) decoder_1 (
    .out0(main_1_p2[0]), .out1(main_1_p2[1]), .out2(main_1_p2[2]), .out3(main_1_p2[3]), .out4(main_1_p2[4]),
    .out5(main_1_p2[5]), .out6(main_1_p2[6]), .out7(main_1_p2[7]), .out8(main_1_p2[8]), .out9(main_1_p2[9]),
    .out10(main_1_p2[10]), .out11(main_1_p2[11]), .out12(main_1_p2[12]), .out13(main_1_p2[13]),
    .out14(main_1_p2[14]), .out15(main_1_p2[15]), .sel(counter_3_q));  // open: en
  Demultiplexer #(.select(4), .width(16)) demultiplexer_1 (
    .out0(main_1_p4), .out1(main_1_p6), .out2(main_1_p8), .out3(main_1_p10), .out4(main_1_p12),
    .out5(main_1_p14), .out6(main_1_p16), .out7(main_1_p18), .out8(main_1_p20), .out9(main_1_p22),
    .out10(main_1_p24), .out11(main_1_p26), .out12(main_1_p28), .out13(main_1_p30), .out14(main_1_p32),
    .out15(main_1_p34), .in(main_1_p2), .sel(counter_1_q));  // open: en

  // Notes on the sheet:
  //   X
  //   contents of rom_1 (hex, n*v repeats v):
  //   0 1 0 1 0 1 0 1 0 1 0 1 0 1 0 1
  //   Y
endmodule

module REGISTER_FILE (
  input  [3:0] in_1,
  input  in_2,
  input  [2:0] in_3,
  input  [2:0] in_4,
  output [3:0] out_5
);

  wire decoder_1_out1, decoder_1_out2, decoder_1_out3, decoder_1_out4, decoder_1_out5, decoder_1_out6,
       decoder_1_out7;
  wire [3:0] register_1_q, register_2_q, register_3_q, register_4_q, register_5_q, register_6_q, register_7_q;

  Register #(.width(4)) register_1 (.D(in_1), .en(decoder_1_out1), .Q(register_1_q), .clk(in_2));  // open: clr
  Register #(.width(4)) register_2 (.D(in_1), .en(decoder_1_out2), .Q(register_2_q), .clk(in_2));  // open: clr
  Multiplexer #(.select(3), .width(4)) multiplexer_1 (
    .in1(register_1_q), .in2(register_2_q), .in3(register_3_q), .in4(register_4_q), .in5(register_5_q),
    .in6(register_6_q), .in7(register_7_q), .out(out_5), .sel(in_3));  // open: in0, en
  Register #(.width(4)) register_3 (.D(in_1), .en(decoder_1_out3), .Q(register_3_q), .clk(in_2));  // open: clr
  Decoder #(.select(3)) decoder_1 (
    .out1(decoder_1_out1), .out2(decoder_1_out2), .out3(decoder_1_out3), .out4(decoder_1_out4),
    .out5(decoder_1_out5), .out6(decoder_1_out6), .out7(decoder_1_out7), .sel(in_4));  // open: out0, en
  Register #(.width(4)) register_4 (.D(in_1), .en(decoder_1_out4), .Q(register_4_q), .clk(in_2));  // open: clr
  Register #(.width(4)) register_5 (.D(in_1), .en(decoder_1_out5), .Q(register_5_q), .clk(in_2));  // open: clr
  Register #(.width(4)) register_6 (.D(in_1), .en(decoder_1_out6), .Q(register_6_q), .clk(in_2));  // open: clr
  Register #(.width(4)) register_7 (.D(in_1), .en(decoder_1_out7), .Q(register_7_q), .clk(in_2));  // open: clr
endmodule

module SCREEN_REGISTER (
  input  in_1,
  input  in_2,
  input  [15:0] in_3,
  input  [15:0] in_4,
  input  [15:0] in_5,
  input  [15:0] in_6,
  input  [15:0] in_7,
  input  [15:0] in_8,
  input  [15:0] in_9,
  input  [15:0] in_10,
  input  [15:0] in_11,
  input  [15:0] in_12,
  input  [15:0] in_13,
  input  [15:0] in_14,
  input  [15:0] in_15,
  input  [15:0] in_16,
  input  [15:0] in_17,
  input  [15:0] in_18,
  output [15:0] out_19,
  output [15:0] out_20,
  output [15:0] out_21,
  output [15:0] out_22,
  output [15:0] out_23,
  output [15:0] out_24,
  output [15:0] out_25,
  output [15:0] out_26,
  output [15:0] out_27,
  output [15:0] out_28,
  output [15:0] out_29,
  output [15:0] out_30,
  output [15:0] out_31,
  output [15:0] out_32,
  output [15:0] out_33,
  output [15:0] out_34
);

  wire [15:0] or_1_out, or_2_out, or_3_out, or_4_out, or_5_out, or_6_out, or_7_out, or_8_out, or_9_out,
       or_10_out, or_11_out, or_12_out, or_13_out, or_14_out, or_15_out, or_16_out;

  assign or_1_out = in_3 | out_19;  // OR_Gate or_1, 16 bits wide
  Register #(.width(16), .trigger("high")) register_1 (.D(or_1_out), .Q(out_19), .clk(in_1), .clr(in_2));  // open: en
  assign or_2_out = in_4 | out_20;  // OR_Gate or_2, 16 bits wide
  Register #(.width(16), .trigger("high")) register_2 (.D(or_2_out), .Q(out_20), .clk(in_1), .clr(in_2));  // open: en
  assign or_3_out = in_5 | out_21;  // OR_Gate or_3, 16 bits wide
  Register #(.width(16), .trigger("high")) register_3 (.D(or_3_out), .Q(out_21), .clk(in_1), .clr(in_2));  // open: en
  assign or_4_out = in_6 | out_22;  // OR_Gate or_4, 16 bits wide
  Register #(.width(16), .trigger("high")) register_4 (.D(or_4_out), .Q(out_22), .clk(in_1), .clr(in_2));  // open: en
  Register #(.width(16), .trigger("high")) register_5 (.D(or_5_out), .Q(out_23), .clk(in_1), .clr(in_2));  // open: en
  assign or_5_out = in_7 | out_23;  // OR_Gate or_5, 16 bits wide
  Register #(.width(16), .trigger("high")) register_6 (.D(or_6_out), .Q(out_24), .clk(in_1), .clr(in_2));  // open: en
  assign or_6_out = in_8 | out_24;  // OR_Gate or_6, 16 bits wide
  Register #(.width(16), .trigger("high")) register_7 (.D(or_7_out), .Q(out_25), .clk(in_1), .clr(in_2));  // open: en
  assign or_7_out = in_9 | out_25;  // OR_Gate or_7, 16 bits wide
  Register #(.width(16), .trigger("high")) register_8 (.D(or_8_out), .Q(out_26), .clk(in_1), .clr(in_2));  // open: en
  assign or_8_out = in_10 | out_26;  // OR_Gate or_8, 16 bits wide
  assign or_9_out = in_11 | out_27;  // OR_Gate or_9, 16 bits wide
  Register #(.width(16), .trigger("high")) register_9 (.D(or_9_out), .Q(out_27), .clk(in_1), .clr(in_2));  // open: en
  assign or_10_out = in_12 | out_28;  // OR_Gate or_10, 16 bits wide
  Register #(.width(16), .trigger("high")) register_10 (.D(or_10_out), .Q(out_28), .clk(in_1), .clr(in_2));  // open: en
  assign or_11_out = in_13 | out_29;  // OR_Gate or_11, 16 bits wide
  Register #(.width(16), .trigger("high")) register_11 (.D(or_11_out), .Q(out_29), .clk(in_1), .clr(in_2));  // open: en
  assign or_12_out = in_14 | out_30;  // OR_Gate or_12, 16 bits wide
  Register #(.width(16), .trigger("high")) register_12 (.D(or_12_out), .Q(out_30), .clk(in_1), .clr(in_2));  // open: en
  Register #(.width(16), .trigger("high")) register_13 (.D(or_13_out), .Q(out_31), .clk(in_1), .clr(in_2));  // open: en
  assign or_13_out = in_15 | out_31;  // OR_Gate or_13, 16 bits wide
  Register #(.width(16), .trigger("high")) register_14 (.D(or_14_out), .Q(out_32), .clk(in_1), .clr(in_2));  // open: en
  assign or_14_out = in_16 | out_32;  // OR_Gate or_14, 16 bits wide
  Register #(.width(16), .trigger("high")) register_15 (.D(or_15_out), .Q(out_33), .clk(in_1), .clr(in_2));  // open: en
  assign or_15_out = in_17 | out_33;  // OR_Gate or_15, 16 bits wide
  Register #(.width(16), .trigger("high")) register_16 (.D(or_16_out), .Q(out_34), .clk(in_1), .clr(in_2));  // open: en
  assign or_16_out = in_18 | out_34;  // OR_Gate or_16, 16 bits wide
endmodule

module ALU (
  input  [3:0] in_1,
  input  [3:0] in_2,
  input  in_3,
  output [3:0] out_4
);

  wire [3:0] adder_1_out, subtractor_1_out;

  Subtractor #(.width(4)) subtractor_1 (.a(in_1), .b(in_2), .out(subtractor_1_out));  // open: bin, bout
  Adder #(.width(4)) adder_1 (.a(in_1), .b(in_2), .out(adder_1_out));  // open: cin, cout
  Multiplexer #(.width(4)) multiplexer_1 (
    .in0(adder_1_out), .in1(subtractor_1_out), .out(out_4), .sel(in_3));  // open: en
endmodule
