// Logisim project FINAL GPU.circ as structural Verilog
module ALU (
  input  [3:0] in_1,
  input  [3:0] in_2
);

  wire [3:0] adder_1_out, subtractor_1_out, undriven, undriven_2;

  Subtractor #(.width(4)) subtractor_1 (.a(undriven), .b(undriven_2), .out(subtractor_1_out));  // open: bin, bout
  Adder #(.width(4)) adder_1 (.a(in_1), .b(undriven_2), .out(adder_1_out));  // open: cin, cout
  ALU alu_1 ();  // open: in_1, in_2
endmodule
