// Logisim project GPU.circ as structural Verilog: 2 circuits, main circuit main
module main (
  input  [3:0] in_1,
  input  [3:0] in_2,
  output [3:0] out_3
);

  wire [3:0] adder_1_out, subtractor_1_out;

  ALU alu_1 ();
  ALU alu_2 ();
  ALU alu_3 ();
  ALU alu_4 ();
  ALU alu_5 ();
  ALU alu_6 ();
  ALU alu_7 ();
  ALU alu_8 ();
  ALU alu_9 ();
  ALU alu_10 ();
  ALU alu_11 ();
  ALU alu_12 ();
  ALU alu_13 ();
  ALU alu_14 ();
  ALU alu_15 ();
  ALU alu_16 ();
  Subtractor #(.width(4)) subtractor_1 (.a(in_1), .b(in_2), .out(subtractor_1_out));  // open: bin, bout
  Adder #(.width(4)) adder_1 (.a(in_1), .b(in_2), .out(adder_1_out));  // open: cin, cout
  ALU alu_17 ();
  ALU alu_18 ();
  ALU alu_19 ();
  ALU alu_20 ();
  ALU alu_21 ();
  Multiplexer #(.width(4)) multiplexer_1 (.in0(adder_1_out), .in1(subtractor_1_out), .out(out_3));  // open: sel, en
  ALU alu_22 ();
  ALU alu_23 ();
  ALU alu_24 ();
endmodule

module ALU (
);

  wire undriven_3;
  wire [1:0] undriven;
  wire [3:0] register_1_q, register_2_q, undriven_2;
  wire [15:0] decoder_1_out0;

  Register #(.width(4)) register_1 (.D(undriven_2), .en(undriven[0]), .Q(register_1_q), .clk(undriven_3));  // open: clr
  Register #(.width(4)) register_2 (.D(undriven_2), .en(undriven[1]), .Q(register_2_q), .clk(undriven_3));  // open: clr
  ALU alu_1 ();
  Demultiplexer #(.select(4), .width(16)) demultiplexer_1 (
    .in(decoder_1_out0), .sel(register_1_q));  // open: out0, out1, out2, out3, out4, out5, out6, out7, out8, out9, out10, out11, out12, out13, out14, out15, en
  Decoder #(.select(4)) decoder_1 (
    .out0(decoder_1_out0[0]), .out1(decoder_1_out0[1]), .out2(decoder_1_out0[2]), .out3(decoder_1_out0[3]),
    .out4(decoder_1_out0[4]), .out5(decoder_1_out0[5]), .out6(decoder_1_out0[6]), .out7(decoder_1_out0[7]),
    .out8(decoder_1_out0[8]), .out9(decoder_1_out0[9]), .out10(decoder_1_out0[10]),
    .out11(decoder_1_out0[11]), .out12(decoder_1_out0[12]), .out13(decoder_1_out0[13]),
    .out14(decoder_1_out0[14]), .out15(decoder_1_out0[15]), .sel(register_2_q));  // open: en
endmodule
